# Fritzing sketch esp32c3-doorbell (saved by Fritzing 1.0.3b)

parts:
  A1 = Esp32-c3 super mini
  S1 = Pushbutton [package="[THT]"]

nets:
  N1: A1.Pin_12, S1.Pin_3, S1.Pin_4
  N2: A1.Pin_15, S1.Pin_1, S1.Pin_2

custom parts:
  Esp32-c3 super mini: ESP32-C3 Development Board ESP32 SuperMini Development Board ESP32 Development Board WiFi Bluetooth.
